# Fritzing sketch XbeeFixedNode (saved by Fritzing 0.9.2b)

parts:
  Componente1 = Arduino XBee Shield
  U1 = XBEE-1 [package=xbee-silk]
  Componente2 = Arduino Uno (Rev3)

nets:
  N1: Componente1.D7, Componente2.D8
  N2: Componente1.N$27, U1.DIO4
