# Fritzing sketch Xbeelilypad (saved by Fritzing 0.9.2b)

parts:
  Componente2 = LilyPad XBee
  Componente3 = Lilypad Arduino Board
  U1 = XBEE-1 [package=xbee-silk]  # not connected

nets:
  3.3V: Componente2.3.3V, Componente3.VCC
  GND: Componente2.GND, Componente3.GND
  N1: Componente2.TX-O, Componente3.D2
  N2: Componente2.RX-I, Componente3.D3
  N3: Componente2.RSSI, Componente3.D6
